// Logisim project Osnova8_CPU.circ as structural Verilog: 2 circuits, main circuit CPU_Osnova8
module main (
  input  FLG,
  output [3:0] out_2,
  output [3:0] out_3,
  output [7:0] out_4,
  output [7:0] out_5,
  output [3:0] out_6,
  output [3:0] out_7,
  output [7:0] out_8,
  output [7:0] out_9,
  output [3:0] out_10,
  output [3:0] out_11,
  output [3:0] out_12,
  output [3:0] out_13,
  output [3:0] out_14,
  output [3:0] out_15,
  output [3:0] out_16,
  output [3:0] out_17,
  output [3:0] out_18,
  output [3:0] out_19,
  output [3:0] out_20,
  output [3:0] out_21,
  output [3:0] out_22,
  output [3:0] out_23,
  output [3:0] out_24,
  output [3:0] out_25,
  output [3:0] out_26,
  output [3:0] out_27,
  output [3:0] out_28,
  output [3:0] out_29,
  output [7:0] out_30,
  output [3:0] out_31,
  output [7:0] out_32,
  output [3:0] out_33
);

  wire clock_1_out, INT_out, MAIN_CPU_read, not_1_out, not_2_out;
  wire [7:0] MAIN_CPU_adbl, MAIN_CPU_db_out, MAIN_ROM_data;

  Clock clock_1 (.out(clock_1_out));
  not not_1 (not_1_out, INT_out);
  Button INT (.out(INT_out));
  CPU_Osnova8 MAIN_CPU (
    .EN1(1'b1), .EN2(1'b1), .CLK(clock_1_out), .FLG(FLG), .INTI(not_1_out), .DB_IN(MAIN_CPU_db_out),
    .out_44(out_12), .out_47(out_17), .out_49(out_22), .out_50(out_27), .out_53(out_11), .out_54(out_16),
    .out_55(out_21), .out_56(out_26), .out_28(out_14), .out_31(out_19), .out_34(out_24), .out_36(out_29),
    .out_38(out_13), .out_39(out_18), .out_40(out_23), .out_41(out_28), .out_9(out_7), .out_17(out_6),
    .out_8(out_31), .out_29(out_33), .READ(MAIN_CPU_read), .out_32(out_4), .out_43(out_8),
    .ADBL(MAIN_CPU_adbl), .DB_OUT(MAIN_CPU_db_out), .out_10(out_30), .out_16(out_10), .out_19(out_15),
    .out_21(out_20), .out_23(out_25), .out_46(out_5), .out_52(out_9), .out_35(out_3), .out_42(out_2),
    .out_7(out_32));  // open: out_48, out_33, WRITE, T8CLK, T16CLK, DONE, BUSY, INTX, ADBH, ADBS, SELP, out_45, out_51, out_30, out_37
  ROM MAIN_ROM (.addr(MAIN_CPU_adbl), .data(MAIN_ROM_data));
  not not_2 (not_2_out, MAIN_CPU_read);
  assign MAIN_CPU_db_out = not_2_out ? MAIN_ROM_data : 8'bz;  // Controlled_Buffer controlled_buffer_1

  // Notes on the sheet:
  //   contents of MAIN_ROM (hex, n*v repeats v):
  //   0 8c 97
endmodule

module CPU_Osnova8 (
  input  EN1,
  input  EN2,
  input  CLK,
  input  [7:0] DB_IN,
  input  FLG,
  input  INTI,
  output [7:0] out_7,
  output [3:0] out_8,
  output [3:0] out_9,
  output [7:0] out_10,
  output READ,
  output [7:0] ADBL,
  output WRITE,
  output [7:0] ADBH,
  output [3:0] ADBS,
  output [3:0] out_16,
  output [3:0] out_17,
  output T8CLK,
  output [3:0] out_19,
  output T16CLK,
  output [3:0] out_21,
  output [7:0] DB_OUT,
  output [3:0] out_23,
  output DONE,
  output BUSY,
  output [1:0] SELP,
  output INTX,
  output [3:0] out_28,
  output [3:0] out_29,
  output [3:0] out_30,
  output [3:0] out_31,
  output [7:0] out_32,
  output [7:0] out_33,
  output [3:0] out_34,
  output [3:0] out_35,
  output [3:0] out_36,
  output [3:0] out_37,
  output [3:0] out_38,
  output [3:0] out_39,
  output [3:0] out_40,
  output [3:0] out_41,
  output [3:0] out_42,
  output [7:0] out_43,
  output [3:0] out_44,
  output [3:0] out_45,
  output [7:0] out_46,
  output [3:0] out_47,
  output [7:0] out_48,
  output [3:0] out_49,
  output [3:0] out_50,
  output [3:0] out_51,
  output [7:0] out_52,
  output [3:0] out_53,
  output [3:0] out_54,
  output [3:0] out_55,
  output [3:0] out_56
);

  wire ACT_INCP, ACT_INCPH, ACT_INCPH_N, ACT_INCPL, ACT_INCPL_N, ACT_INT, ACT_OPC, ALU_L_co, ARG_ADD,
       ARG_ALU, ARG_DVR, ARG_PFH, ARG_PFL, ARG_RC, ARG_RESR, ARG_SFPS, BUS_CIN, BUS_M, CU_AND_A_q, CU_DCD_y3,
       CU_DCD_y5, FLG_AEQB_H, FLG_AEQB_L, FLG_CARRY, FLG_NEG, FLG_ODD, OPC_DVRH, OPC_DVRL, OPC_DVRR,
       OPC_INTSI, OPC_JMP, OPC_PFH, OPC_PFL, OPC_PS, OPC_RA, OPC_RB, OPC_RC, OPC_RESR, OPC_SF, PFC_AND_A_q,
       PFC_AND_B_q, PFC_MUL_w, PFC_NAND_A_q, PFH_ADR_L_co, PFL_ADR_L_co, STG_JMP, STG_PC, STG_PC_BR,
       STG_PC_BR_N, STG_PC_N, STG_PFH_CIN, STG_PFL_CIN;
  wire [1:0] BUS_PRA, BUS_PWA;
  wire [2:0] ALU_H_f;
  wire [3:0] BUS_ARG, BUS_OPC, BUS_S, CU_CNT_q, PFH_ADR_L_sum, PFL_ADR_L_sum;
  wire [3:1] ALU_L_f, SFPS_INTC_q;
  wire [7:0] ALU_RA_o, ALU_RB_o, PFH_REG_o, PFL_REG_o, SFPS_PS_o;
  wire [7:4] PFH_ADR_H_sum, PFL_ADR_H_sum, SFPS_INSTM_y, SFPS_PCM_y;
  wire [7:6] IEU_DVR_H_q;

  IC_74161 SFPS_INTC (
    .LD(1'b0), .D(4'b1111), .CLK(ACT_INT), .CLR(DONE), .ENT(1'b1), .ENP(1'b1), .val(out_8),
    .Q({SFPS_INTC_q, BUSY}));  // open: CO
  IC_74374 SFPS_PS (
    .D({DB_IN[7:4], 4'b1111}), .CP(OPC_PS), .OE(1'b0), .O({SFPS_PS_o[7:6], SELP, SFPS_PS_o[3:0]}),
    .val(out_10));
  IC_74670 SFPS_SF (
    .WA(BUS_PWA), .WE(OPC_SF), .D(DB_IN[3:0]), .RE(1'b0), .RA(BUS_PRA), .val3(out_23), .val2(out_21),
    .Q(ADBS), .val1(out_19), .val0(out_16));
  IC_74374 ALU_RA (.D(DB_IN), .CP(OPC_RA), .OE(1'b0), .O(ALU_RA_o), .val(out_32));
  IC_74374 ALU_RB (.D(DB_IN), .CP(OPC_RB), .OE(1'b0), .O(ALU_RB_o), .val(out_43));
  IC_74181 ALU_L (
    .A(ALU_RA_o[3:0]), .S(BUS_S), .CIN(BUS_CIN), .M(BUS_M), .B(ALU_RB_o[3:0]), .AEQB(FLG_AEQB_L),
    .CO(ALU_L_co), .val(out_35), .F({ALU_L_f, FLG_ODD}));  // open: G, P
  IC_74181 ALU_H (
    .A(ALU_RA_o[7:4]), .S(BUS_S), .CIN(ALU_L_co), .M(BUS_M), .B(ALU_RB_o[7:4]), .AEQB(FLG_AEQB_H),
    .CO(FLG_CARRY), .val(out_42), .F({FLG_NEG, ALU_H_f}));  // open: G, P
  IC_74374 ALU_RC (.D(DB_IN), .CP(OPC_RC), .OE(ARG_RC), .O(DB_OUT), .val(out_46));
  IC_74374 ALU_RESR (.D(DB_IN), .CP(OPC_RESR), .OE(ARG_RESR), .O(DB_OUT), .val(out_52));
  IC_74541 SFPS_PCM (
    .I({4'b1111, BUSY, 1'b0, BUSY, 1'b0}), .OE1(STG_PC), .OE2(1'b0), .Y({SFPS_PCM_y, BUS_PWA, BUS_PRA}));
  IC_74541 SFPS_INSTM (
    .I({4'b1111, SFPS_PS_o[7:6], SELP}), .OE1(STG_PC_N), .OE2(1'b0), .Y({SFPS_INSTM_y, BUS_PWA, BUS_PRA}));
  IC_74541 SFPS_BUF (.I({SFPS_PS_o[7:6], SELP, ADBS}), .OE1(ARG_SFPS), .OE2(1'b0), .Y(DB_OUT));
  IC_74541 ALU_BUF (.I({FLG_NEG, ALU_H_f, ALU_L_f, FLG_ODD}), .OE1(ARG_ALU), .OE2(1'b0), .Y(DB_OUT));
  IC_74374 IEU_IR (.D(DB_IN), .CP(T8CLK), .OE(1'b0), .O({BUS_OPC, BUS_ARG}), .val(out_7));
  IC_74138 IEU_DCD_OPC_H (
    .EN3(ACT_OPC), .D(BUS_OPC[2:0]), .EN1(BUS_OPC[3]), .EN2(1'b0), .Y0(OPC_DVRL), .Y1(OPC_DVRH), .Y2(OPC_RA),
    .Y3(OPC_RB), .Y4(OPC_PS), .Y5(OPC_INTSI), .Y6(INTX), .Y7(DONE));
  IC_74283 PFL_ADR_L (
    .CIN(STG_PFL_CIN), .A(ADBL[3:0]), .B(4'b0000), .CO(PFL_ADR_L_co), .val(out_30), .SUM(PFL_ADR_L_sum));
  IC_74283 PFL_ADR_H (
    .CIN(PFL_ADR_L_co), .A(ADBL[7:4]), .B(4'b0000), .CO(STG_PFH_CIN), .val(out_37), .SUM(PFL_ADR_H_sum));
  IC_74283 PFH_ADR_L (
    .CIN(STG_PFH_CIN), .A(ADBH[3:0]), .B(4'b0000), .CO(PFH_ADR_L_co), .val(out_45), .SUM(PFH_ADR_L_sum));
  IC_74283 PFH_ADR_H (.CIN(PFH_ADR_L_co), .A(ADBH[7:4]), .B(4'b0000), .val(out_51), .SUM(PFH_ADR_H_sum));  // open: CO
  IC_74138 IEU_DCD_OPC_L (
    .EN3(ACT_OPC), .D(BUS_OPC[2:0]), .EN1(1'b1), .EN2(BUS_OPC[3]), .Y0(OPC_JMP), .Y1(OPC_RC), .Y2(OPC_SF),
    .Y3(OPC_PFL), .Y4(OPC_PFH), .Y5(OPC_RESR), .Y6(WRITE), .Y7(OPC_DVRR));
  IC_74138 IEU_DCD_SENSE (
    .EN3(STG_PC_N), .D(BUS_OPC[2:0]), .EN1(1'b1), .EN2(BUS_OPC[3]), .Y0(STG_JMP));  // open: Y1, Y2, Y3, Y4, Y5, Y6, Y7
  IC_74374 PFL_REG (.D({PFL_ADR_H_sum, PFL_ADR_L_sum}), .CP(ACT_INCPL_N), .OE(STG_PC_BR), .O(PFL_REG_o), .val(out_33));
  IC_74541 PFL_BUF_IN (.I(DB_IN), .OE1(STG_PC_BR_N), .OE2(1'b0), .Y(PFL_REG_o));
  IC_74374 PFH_REG (.D({PFH_ADR_H_sum, PFH_ADR_L_sum}), .CP(ACT_INCPH_N), .OE(STG_PC_BR), .O(PFH_REG_o), .val(out_48));
  IC_74541 PFH_BUF_IN (.I(DB_IN), .OE1(STG_PC_BR_N), .OE2(1'b0), .Y(PFH_REG_o));
  IC_74670 PFL_L (
    .WA(BUS_PWA), .WE(ACT_INCPL), .D(PFL_REG_o[3:0]), .RE(1'b0), .RA(BUS_PRA), .val3(out_36), .val2(out_34),
    .Q(ADBL[3:0]), .val1(out_31), .val0(out_28));
  IC_74670 PFL_H (
    .WA(BUS_PWA), .WE(ACT_INCPL), .D(PFL_REG_o[7:4]), .RE(1'b0), .RA(BUS_PRA), .val3(out_41), .val2(out_40),
    .Q(ADBL[7:4]), .val1(out_39), .val0(out_38));
  IC_74670 PFH_L (
    .WA(BUS_PWA), .WE(ACT_INCPH), .D(PFH_REG_o[3:0]), .RE(1'b0), .RA(BUS_PRA), .val3(out_50), .val2(out_49),
    .Q(ADBH[3:0]), .val1(out_47), .val0(out_44));
  IC_74670 PFH_H (
    .WA(BUS_PWA), .WE(ACT_INCPH), .D(PFH_REG_o[7:4]), .RE(1'b0), .RA(BUS_PRA), .val3(out_56), .val2(out_55),
    .Q(ADBH[7:4]), .val1(out_54), .val0(out_53));
  IC_74138 IEU_DCD_ARG (
    .EN3(STG_PC_BR_N), .D(BUS_ARG[2:0]), .EN1(1'b1), .EN2(BUS_ARG[3]), .Y0(ARG_ALU), .Y1(ARG_RC),
    .Y2(ARG_SFPS), .Y3(ARG_PFL), .Y4(ARG_PFH), .Y5(ARG_RESR), .Y6(ARG_ADD), .Y7(ARG_DVR));
  IC_74161 IEU_DVR_L (
    .LD(1'b0), .D(BUS_ARG), .CLK(OPC_DVRL), .CLR(OPC_DVRR), .ENT(1'b0), .ENP(1'b0), .val(out_9), .Q(BUS_S));  // open: CO
  IC_74161 IEU_DVR_H (
    .LD(1'b0), .D(BUS_ARG), .CLK(OPC_DVRH), .CLR(OPC_DVRR), .ENT(1'b0), .ENP(1'b0), .val(out_17),
    .Q({IEU_DVR_H_q, BUS_CIN, BUS_M}));  // open: CO
  IC_74541 PFL_BUF_OUT (.I(ADBL), .OE1(ARG_PFL), .OE2(1'b0), .Y(DB_OUT));
  IC_74541 PFH_BUF_OUT (.I(ADBH), .OE1(ARG_PFL), .OE2(1'b0), .Y(DB_OUT));
  IC_74541 IEU_DVR_BUF (.I({IEU_DVR_H_q, BUS_CIN, BUS_M, BUS_S}), .OE1(ARG_DVR), .OE2(1'b0), .Y(DB_OUT));
  IC_7408 PFC_AND_A (.A(FLG_AEQB_L), .B(FLG_AEQB_H), .Q(PFC_AND_A_q));
  IC_7400 PFC_NAND_A (.A(FLG_CARRY), .B(FLG_CARRY), .Q(PFC_NAND_A_q));
  IC_74161 CU_CNT (
    .LD(1'b1), .D(4'b1111), .CLK(CLK), .CLR(1'b1), .ENT(EN1), .ENP(EN2), .val(out_29), .Q(CU_CNT_q),
    .CO(T16CLK));
  IC_74151 PFC_MUL (
    .S(BUS_ARG[2:0]), .D0(1'b1), .D1(PFC_AND_A_q), .D2(FLG), .D3(BUSY), .D4(PFC_NAND_A_q), .D5(FLG_NEG),
    .D6(FLG_ODD), .D7(1'b0), .EN(OPC_JMP), .W(PFC_MUL_w));  // open: Y
  IC_74138 CU_DCD (
    .EN3(1'b0), .D(CU_CNT_q[2:0]), .EN1(1'b1), .EN2(1'b0), .Y1(T8CLK), .Y3(CU_DCD_y3), .Y4(ACT_OPC),
    .Y5(CU_DCD_y5), .Y7(ACT_INCP));  // open: Y0, Y2, Y6
  IC_7408 CU_AND_A (.A(CU_DCD_y3), .B(ACT_OPC), .Q(CU_AND_A_q));
  IC_7408 PFC_AND_B (.A(ACT_INCP), .B(PFC_MUL_w), .Q(PFC_AND_B_q));
  IC_7400 PFC_NAND_D (.A(INTI), .B(OPC_INTSI), .Q(ACT_INT));
  IC_7400 CU_NAND_A (.A(CU_AND_A_q), .B(CU_DCD_y5), .Q(STG_PC));
  IC_7408 CU_AND_D (.A(1'b1), .B(1'b1));  // open: Q
  IC_7408 PFC_AND_C (.A(OPC_PFL), .B(PFC_AND_B_q), .Q(ACT_INCPL));
  IC_7408 PFC_AND_D (.A(PFC_AND_B_q), .B(OPC_PFH), .Q(ACT_INCPH));
  IC_7400 PFC_NAND_B (.A(ACT_INCPL), .B(ACT_INCPL), .Q(ACT_INCPL_N));
  IC_7400 PFC_NAND_C (.A(ACT_INCPH), .B(ACT_INCPH), .Q(ACT_INCPH_N));
  IC_7408 CU_AND_B (.A(STG_PC), .B(STG_JMP), .Q(STG_PC_BR));
  IC_7408 CU_AND_C (.A(ARG_ADD), .B(STG_PC_BR), .Q(READ));
  IC_7400 CU_NAND_B (.A(STG_PC_BR), .B(STG_PC_BR), .Q(STG_PC_BR_N));
  IC_7400 CU_NAND_C (.A(STG_PC), .B(STG_PC), .Q(STG_PC_N));
  IC_7400 CU_NAND_D (.A(STG_PC), .B(BUS_ARG[3]), .Q(STG_PFL_CIN));

  // Other names for the same wires on the sheet: FLG_INTM_N = BUSY; BUS_ADS[3:0] = ADBS; BUS_SELP[1:0] = SELP;
  //   ACT_IR = T8CLK; ADD_R = READ; BUS_ADH[7:0] = ADBH; BUS_ADL[7:0] = ADBL; BUS_DATA_IN[7:0] = DB_IN;
  //   BUS_DATA_OUT[7:0] = DB_OUT; BUS_INT = INTI; FLG_X_N = FLG; OPC_ADD = WRITE; OPC_INTE = DONE; OPC_INTSX = INTX;
  //   STG_ODDCYC = T16CLK

  // Notes on the sheet:
  //   ACT - cmbl action
  //   STG - cmbl stage
  //   BUS - bus values
  //   OPC - inst opcodes
  //   ARG - inst arguments
  //   FLG - flags -> jmp conditions
  //   Osnova8 CPU - 28. April, 2026. by Ivan Jonjic (IJPantic on github)
endmodule
